// Logisim project LabN1.circ as structural Verilog: 1 circuit, main circuit main
module main (
  input  Sel_1_0,
  input  In_1_0,
  input  In_1_1,
  input  Sel_2_0,
  input  Sel_2_1,
  input  In_2_0,
  input  In_2_1,
  input  In_2_2,
  input  In_2_3,
  output Out_1,
  output out_11
);

  wire and_1_out, and_2_out, and_3_out, and_4_out, and_5_out, and_6_out, not_1_out, not_2_out, not_3_out,
       not_4_out, not_5_out, not_6_out;

  not not_1 (not_1_out, Sel_1_0);
  not not_2 (not_2_out, Sel_2_0);
  not not_3 (not_3_out, Sel_2_1);
  not not_4 (not_4_out, not_1_out);
  not not_5 (not_5_out, not_2_out);
  not not_6 (not_6_out, not_3_out);
  and and_1 (and_1_out, not_4_out, In_1_0);
  and and_2 (and_2_out, not_1_out, In_1_1);
  or or_1 (Out_1, and_1_out, and_2_out);
  and and_3 (and_3_out, not_2_out, In_2_0, not_3_out);
  and and_4 (and_4_out, not_2_out, In_2_1, not_6_out);
  and and_5 (and_5_out, not_5_out, In_2_2, not_3_out);
  and and_6 (and_6_out, not_5_out, In_2_3, not_6_out);
  or or_2 (out_11, and_3_out, and_4_out, and_5_out, and_6_out);

  // Notes on the sheet:
  //   Zhan Hodzhabergenov, LabN1, Date: Feb 3, 2025
endmodule
