// Logisim project LabN3.circ as structural Verilog: 1 circuit, main circuit main
module main (
  input  In1,
  input  In2,
  input  In3,
  input  In4,
  input  In5,
  input  In6,
  input  In7,
  input  In8,
  input  In9,
  output out_10,
  output out_11,
  output out_12,
  output out_13
);

  wire U1_out, U2_out, U3_out, U4_out, U5_out, U6_out, U7_out, U8_out, U9_out, U10_out, U11_out, U12_out,
       U16_out;

  nor U16 (U16_out, In8, In9);
  and U1 (U1_out, In1, ~In2, ~In4, ~In6, U16_out);  // AND_Gate
  and U2 (U2_out, In3, ~In4, ~In6, U16_out);  // AND_Gate
  and U3 (U3_out, In5, ~In6, U16_out);  // AND_Gate
  and U4 (U4_out, U16_out, In7);
  and U5 (U5_out, In2, ~In4, ~In5, U16_out);  // AND_Gate
  and U6 (U6_out, ~In4, ~In5, In3, U16_out);  // AND_Gate
  and U7 (U7_out, In6, U16_out);
  and U8 (U8_out, In7, U16_out);
  and U9 (U9_out, In4, U16_out);
  and U10 (U10_out, In5, U16_out);
  buf U11 (U11_out, In6);  // AND_Gate
  and U12 (U12_out, In7, U16_out);
  or U13 (out_10, U1_out, U2_out, U3_out, U4_out, In9);
  or U14 (out_11, U5_out, U6_out, U7_out, U8_out);
  or U15 (out_12, U9_out, U10_out, U11_out, U12_out);
  or U17 (out_13, In8, In9);

  // Notes on the sheet:
  //   Zhan Hodzhabergenov, LabN3, date: Feb 3, 2025
endmodule
