// Logisim project LabN2.circ as structural Verilog: 1 circuit, main circuit main
module main (
  input  A1,
  input  B1,
  input  C1,
  input  A2,
  input  B2,
  input  C2,
  input  D2,
  output out_8,
  output out_9
);

  wire and_1_out, and_2_out, and_3_out, and_4_out, and_5_out, and_6_out, and_7_out;

  and and_1 (and_1_out, ~A1, B1, ~C1);  // AND_Gate
  and and_2 (and_2_out, A1, ~B1, ~C1);  // AND_Gate
  and and_3 (and_3_out, ~A1, B1, ~C1);  // AND_Gate
  and and_4 (and_4_out, ~A2, ~B2, C2, ~D2);  // AND_Gate
  and and_5 (and_5_out, ~A2, B2, C2, D2);  // AND_Gate
  and and_6 (and_6_out, A2, ~B2, C2, ~D2);  // AND_Gate
  and and_7 (and_7_out, A2, B2, C2, ~D2);  // AND_Gate
  or or_1 (out_8, and_1_out, and_2_out, and_3_out);
  or or_2 (out_9, and_5_out, and_4_out, and_7_out, and_6_out);

  // Notes on the sheet:
  //   Zhan Hodzhabergenov, LabN2, Date: Feb 3, 2025
endmodule
