// Logisim project Lab5.circ as structural Verilog: 7 circuits, main circuit main
module main (
  input  rst,
  input  [1:0] selector,
  output [3:0] Probe1
);

  wire clk_out;

  Clock sysclk ();  // open: out
  Clock clk (.out(clk_out));
  Hex_Digit_Display hex_digit_display_1 (.value(Probe1));  // open: dp
  Universal universal_1 (.clk(clk_out), .rst(rst), .selector(selector), .out_4(Probe1));
endmodule

module Up (
  input  clk,
  input  rst,
  output [3:0] out_3
);

  wire d_ff_1_qn, d_ff_2_qn, d_ff_3_qn, d_ff_4_qn;

  D_Flip_Flop d_ff_1 (.D(d_ff_1_qn), .clk(clk), .Q(out_3[0]), .Qn(d_ff_1_qn), .reset(rst));  // open: preset
  D_Flip_Flop d_ff_2 (.D(d_ff_2_qn), .clk(d_ff_1_qn), .Q(out_3[1]), .Qn(d_ff_2_qn), .reset(rst));  // open: preset
  D_Flip_Flop d_ff_3 (.D(d_ff_3_qn), .clk(d_ff_2_qn), .Q(out_3[2]), .Qn(d_ff_3_qn), .reset(rst));  // open: preset
  D_Flip_Flop d_ff_4 (.D(d_ff_4_qn), .clk(d_ff_3_qn), .Q(out_3[3]), .Qn(d_ff_4_qn), .reset(rst));  // open: preset
endmodule

module Down (
  input  clk,
  input  rst,
  output [3:0] out_3
);

  wire d_ff_1_qn, d_ff_2_qn, d_ff_3_qn, d_ff_4_qn;

  D_Flip_Flop d_ff_1 (.D(d_ff_1_qn), .clk(clk), .Q(out_3[0]), .Qn(d_ff_1_qn), .preset(rst));  // open: reset
  D_Flip_Flop d_ff_2 (.D(d_ff_2_qn), .clk(out_3[0]), .Q(out_3[1]), .Qn(d_ff_2_qn), .preset(rst));  // open: reset
  D_Flip_Flop d_ff_3 (.D(d_ff_3_qn), .clk(out_3[1]), .Q(out_3[2]), .Qn(d_ff_3_qn), .preset(rst));  // open: reset
  D_Flip_Flop d_ff_4 (.D(d_ff_4_qn), .clk(out_3[2]), .Q(out_3[3]), .Qn(d_ff_4_qn), .preset(rst));  // open: reset
endmodule

module Decade (
  input  clk,
  input  rst,
  output [3:0] out_3
);

  wire and_1_out, d_ff_1_qn, d_ff_2_qn, d_ff_3_qn, d_ff_4_qn, or_1_out;

  D_Flip_Flop d_ff_1 (.D(d_ff_1_qn), .clk(clk), .Q(out_3[0]), .Qn(d_ff_1_qn), .reset(or_1_out));  // open: preset
  or or_1 (or_1_out, rst, and_1_out);
  D_Flip_Flop d_ff_2 (.D(d_ff_2_qn), .clk(d_ff_1_qn), .Q(out_3[1]), .Qn(d_ff_2_qn), .reset(or_1_out));  // open: preset
  D_Flip_Flop d_ff_3 (.D(d_ff_3_qn), .clk(d_ff_2_qn), .Q(out_3[2]), .Qn(d_ff_3_qn), .reset(or_1_out));  // open: preset
  D_Flip_Flop d_ff_4 (.D(d_ff_4_qn), .clk(d_ff_3_qn), .Q(out_3[3]), .Qn(d_ff_4_qn), .reset(or_1_out));  // open: preset
  and and_1 (and_1_out, out_3[3], out_3[1]);
endmodule

module Ring (
  input  clk,
  input  rst,
  output [3:0] out_3
);

  D_Flip_Flop d_ff_1 (.D(out_3[3]), .clk(clk), .Q(out_3[0]), .preset(rst));  // open: Qn, reset
  D_Flip_Flop d_ff_2 (.D(out_3[0]), .clk(clk), .Q(out_3[1]), .reset(rst));  // open: Qn, preset
  D_Flip_Flop d_ff_3 (.D(out_3[1]), .clk(clk), .Q(out_3[2]), .reset(rst));  // open: Qn, preset
  D_Flip_Flop d_ff_4 (.D(out_3[2]), .clk(clk), .Q(out_3[3]), .reset(rst));  // open: Qn, preset
endmodule

module Universal (
  input  clk,
  input  rst,
  input  [1:0] selector,
  output [3:0] out_4
);

  wire [3:0] decade_1_out_3, down_1_out_3, ring_1_out_3, up_1_out_3;

  Up up_1 (.clk(clk), .rst(rst), .out_3(up_1_out_3));
  Down down_1 (.clk(clk), .rst(rst), .out_3(down_1_out_3));
  Decade decade_1 (.clk(clk), .rst(rst), .out_3(decade_1_out_3));
  Ring ring_1 (.clk(clk), .rst(rst), .out_3(ring_1_out_3));
  Multiplexer #(.select(2), .width(4)) multiplexer_1 (
    .in0(up_1_out_3), .in1(down_1_out_3), .in2(decade_1_out_3), .in3(ring_1_out_3), .out(out_4),
    .sel(selector));
  Hex_Digit_Display hex_digit_display_1 (.value(out_4));  // open: dp
endmodule

module Johnson (
  input  clk,
  input  rst,
  output [3:0] out_3
);

  wire d_ff_4_qn;

  D_Flip_Flop d_ff_1 (.D(d_ff_4_qn), .clk(clk), .Q(out_3[0]), .preset(rst));  // open: Qn, reset
  D_Flip_Flop d_ff_2 (.D(out_3[0]), .clk(clk), .Q(out_3[1]), .reset(rst));  // open: Qn, preset
  D_Flip_Flop d_ff_3 (.D(out_3[1]), .clk(clk), .Q(out_3[2]), .reset(rst));  // open: Qn, preset
  D_Flip_Flop d_ff_4 (.D(out_3[2]), .clk(clk), .Q(out_3[3]), .Qn(d_ff_4_qn), .reset(rst));  // open: preset
endmodule
